# Fritzing sketch SENSOR MOTOR PLAN (saved by Fritzing 0.9.2b)
breadboards: 1

parts:
  Bauteil1 = Arduino Uno (Rev3)
  M1 = Stepper Motor - Bipolar
  Bauteil2 = EasyDriver_v44
  VCC1 = Battery block 9V
  U1 = AD22100 - Voltage Output Temperature Sensor with Signal Conditioning [part_number=AD22100]

nets:
  N1: Bauteil1.D8, Bauteil2.DIR
  N2: Bauteil1.D9_PWM, Bauteil2.STEP
  N3: Bauteil1.D5_PWM, Bauteil2.ENABLE
  GND: Bauteil1.GND, Bauteil2.GND, Bauteil2.V+, VCC1.-, VCC1.+
  N4: Bauteil1.VIN, U1.Vo
  N5: M1.A, Bauteil2.OUT2A
  N6: M1.C, Bauteil2.OUT2B
  N7: M1.B, Bauteil2.OUT1A
  N8: M1.D, Bauteil2.OUT1B
